# Fritzing sketch Electrical Schematic (saved by Fritzing 0.9.3b)
breadboards: 1

parts:
  RHT1 = Humidity and Temperature Sensor RHT03
  Part2 = Arduino Mega ADK (Rev3)
  J1 = Basic Servo
  R1 = Resistor [tolerance=±5% resistance=220 package=THT]
  LED2 = LED - 5mm [color="Red (633nm)" package="5 mm [THT]"]  # not connected
  Power_plug1 = Power plug
  J2 = Basic Servo
  Raspberry_Pi_1 = Raspberry Pi 3 [part_number=RPI-3-V1.2]
  J3 = Piezo Speaker
  LED9 = LED - 3mm [color="White (6500K)" package="3 mm [THT]"]
  LED10 = LED - 3mm [color="White (6500K)" package="3 mm [THT]"]
  LED_Room_1 = RGB LED - (4 legs) [package="5 mm [THT]"]
  LED_Room_3 = RGB LED - (4 legs) [package="5 mm [THT]"]
  LED_Room_4 = RGB LED - (4 legs) [package="5 mm [THT]"]
  LED_Room_5b = RGB LED - (4 legs) [package="5 mm [THT]"]
  LED_Room_5a = RGB LED - (4 legs) [package="5 mm [THT]"]
  LED_Room_2 = RGB LED - (4 legs) [package="5 mm [THT]"]
  R2 = Resistor [tolerance=±5% resistance=220 package=THT]
  R3 = Resistor [tolerance=±5% resistance=220 package=THT]
  Attic_Fan = DC Motor
  Part3 = Adafruit MiCS-5524 Gas Sensor [part_number="Adafruit #3199"]

nets (from the schematic view):
  N1: RHT1.Vcc, RHT1.Data-signal, RHT1.GND_1, Part2.D3_PWM, LED_Room_1.red_cathode, LED_Room_1.common_anode, LED_Room_3.red_cathode, LED_Room_3.common_anode, LED_Room_4.red_cathode, LED_Room_4.common_anode, LED_Room_5b.red_cathode, LED_Room_5b.common_anode, LED_Room_5a.red_cathode, LED_Room_5a.common_anode, LED_Room_2.red_cathode, LED_Room_2.common_anode
  GND: RHT1.GND_2, Part2.GND, Attic_Fan.pin_2, Part3.GND
  N2: Part2.A8, J3.pin2
  N3: Part2.D19/RX1, Raspberry_Pi_1.GPIO14
  N4: Part2.D18/TX1, Raspberry_Pi_1.GPIO15
  N5: Part2.D13_PWM, R1.Pin_1
  N6: Part2.D10_PWM, LED_Room_1.green_cathode
  N7: Part2.D9_PWM, J1.pulse
  N8: Part2.D8_PWM, J2.pulse
  N9: Part2.D2_PWM, Attic_Fan.pin_1
  N10: Part2.D31, R3.Pin_1
  N11: Part2.D33, R2.Pin_1
  GND_2: J1.gnd, Power_plug1.GND, J2.gnd
  VCC: J1.vcc, Power_plug1.VCC, J2.vcc
  N12: LED9.anode, R3.Pin_0
  N13: LED10.anode, R2.Pin_0
  N14: LED_Room_1.blue_cathode, LED_Room_2.green_cathode
  N15: LED_Room_3.green_cathode, LED_Room_2.blue_cathode
  N16: LED_Room_3.blue_cathode, LED_Room_4.green_cathode
  N17: LED_Room_4.blue_cathode, LED_Room_5a.green_cathode
  N18: LED_Room_5b.green_cathode, LED_Room_5a.blue_cathode

custom parts:
  Adafruit MiCS-5524 Gas Sensor: Give your next sensor project a nose for gasses with the Adafruit MiCS-5524 Gas Sensor Breakout. This breakout makes it easy to use this nice sensor from SGX Sensortech. The MiCS-5524 is a robust MEMS sensor for indoor carbon monoxide and natural gas leakage detection, it's suitable also for indoor air quality monitoring; breath checker and early fire detection. Please note: This sensor is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
